// Logisim project hm7.circ as structural Verilog: 1 circuit, main circuit main
module main (
);

  wire and_2_out, and_3_out, and_4_out, and_5_out, and_6_out, CLK, D0, D1, D2, J0, J1, K0, K1, Q1, Q2, Z;

  D_Flip_Flop d_ff_1 (.clk(CLK), .D(D0), .Q(J0));  // open: Qn, preset, en, reset
  D_Flip_Flop d_ff_2 (.clk(CLK), .D(D1), .Q(Q1));  // open: Qn, preset, en, reset
  and and_1 (D2, ~Q2, Q1, J0, J0);  // AND_Gate
  and and_2 (and_2_out, ~Q2, ~Q1, J0, ~J0);  // AND_Gate
  or or_1 (D1, and_2_out, and_3_out);
  and and_3 (and_3_out, ~Q2, Q1, ~J0, J0);  // AND_Gate
  and and_4 (and_4_out, ~Q2, ~Q1, J0);  // AND_Gate
  and and_5 (and_5_out, ~Q2, Q1, ~J0, J0);  // AND_Gate
  or or_2 (D0, and_4_out, and_5_out, and_6_out);
  and and_6 (and_6_out, Q2, ~Q1, ~J0, J0);  // AND_Gate
  and and_7 (Z, Q2, ~Q1, ~J0);  // AND_Gate
  D_Flip_Flop d_ff_3 (.clk(CLK), .D(D2), .Q(Q2));  // open: Qn, preset, en, reset
  J_K_Flip_Flop j_k_ff_1 (.J(J0), .clk(CLK), .K(K0), .Q(J0));  // open: Qn, preset, en, reset
  and and_8 (J1, J0, ~J0);  // AND_Gate
  or or_3 (K1, J0, ~J0);  // OR_Gate
  not not_1 (K0, J0);
  and and_9 (Z, Q1, J0);
  J_K_Flip_Flop j_k_ff_2 (.J(J1), .clk(CLK), .K(K1), .Q(Q1));  // open: Qn, preset, en, reset

  // Other names for the same wires on the sheet: Q0 = J0; X = J0
endmodule
